// Logisim project snake.circ as structural Verilog: 24 circuits, main circuit main
module main (
);

  wire A_out, and_1_out, and_3_out, and_4_out, and_5_out, and_6_out, and_7_out, Apple_coordinates,
       Apple_found, Apple_initializer, clock_1_out, comparator_1_lt, comparator_2_eq, comparator_3_eq,
       comparator_4_eq, comparator_5_eq, comparator_6_eq, comparator_7_eq, counter_3_carry, counter_6_q,
       D_out, demultiplexer_3_out0, demultiplexer_3_out1, demultiplexer_3_out2, demultiplexer_4_out0,
       demultiplexer_4_out2, demultiplexer_5_out0, demultiplexer_5_out1, Display_clock, Draw_apple,
       Game_Over, Head_increment, Head_position_initializer, Increment_snake_s_length, Initialize_direction,
       Input_controller_reset_keyboard, Length_initializer, M1, M1_Clock, M2, M2_Clock, M3, M3_Clock, M4,
       M4__2, M4_Clock, Main_loop, Memory_clock_M4, multiplexer_5_out, not_1_out, not_2_out, not_3_out,
       Operation_counter_2_q, or_1_out, or_2_out, or_3_out, or_4_out, or_5_out, or_6_out, S_out, W_out,
       You_kinda_won;
  wire [1:0] Module_num, Operation_counter_q;
  wire [1:1] counter_4_q;
  wire [2:0] counter_1_q;
  wire [3:0] apple_coordinate_digit_display_1_out_3, apple_coordinate_digit_display_1_out_4,
       apple_coordinate_digit_display_1_out_5, apple_coordinate_digit_display_1_out_6;
  wire [4:0] Apple_X, Apple_Y, controlled_buffer_3_out, controlled_buffer_4_out, Head_position_X_2_q,
       Head_position_X_q, Head_position_Y_2_q, Head_position_Y_q, multiplexer_3_out, multiplexer_4_out,
       register_1_q, register_2_q, Snake_mover_new_x_coordinate, Snake_mover_new_y_coordinate, X, X__M4,
       X_direction, Y, Y__M4, Y_direction;
  wire [6:0] keyboard_1_data;
  wire [7:0] adder_1_out, Address_for_shifter, Address_q, M3_Address, M4_Address, multiplexer_1_out,
       multiplexer_2_out, Snake_head_position, Snake_length;
  wire [31:0] display_curcuit_32_bits_1_out_7, display_curcuit_32_bits_1_out_8,
       display_curcuit_32_bits_1_out_9, display_curcuit_32_bits_1_out_10, display_curcuit_32_bits_1_out_11,
       display_curcuit_32_bits_1_out_12, display_curcuit_32_bits_1_out_13, display_curcuit_32_bits_1_out_14,
       display_curcuit_32_bits_1_out_15, display_curcuit_32_bits_1_out_16, display_curcuit_32_bits_1_out_17,
       display_curcuit_32_bits_1_out_18, display_curcuit_32_bits_1_out_19, display_curcuit_32_bits_1_out_20,
       display_curcuit_32_bits_1_out_21, display_curcuit_32_bits_1_out_22, display_curcuit_32_bits_1_out_23,
       display_curcuit_32_bits_1_out_24, display_curcuit_32_bits_1_out_25, display_curcuit_32_bits_1_out_26,
       display_curcuit_32_bits_1_out_27, display_curcuit_32_bits_1_out_28, display_curcuit_32_bits_1_out_29,
       display_curcuit_32_bits_1_out_30, display_curcuit_32_bits_1_out_31, display_curcuit_32_bits_1_out_32,
       display_curcuit_32_bits_1_out_33, display_curcuit_32_bits_1_out_34, display_curcuit_32_bits_1_out_35,
       display_curcuit_32_bits_1_out_36, display_curcuit_32_bits_1_out_37, display_curcuit_32_bits_1_out_38;

  Clock clock_1 (.out(clock_1_out));
  Demultiplexer #(.select(3)) demultiplexer_1 (
    .out0(Length_initializer), .out1(Head_position_initializer), .out2(Initialize_direction),
    .out3(Apple_initializer), .out4(Main_loop), .in(clock_1_out), .sel(counter_1_q));  // open: out5, out6, out7, en
  Counter #(.width(3), .max('h7), .trigger("falling")) counter_1 (
    .Q(counter_1_q), .clk(or_2_out), .clr(or_1_out));  // open: load, D, count, carry
  or or_1 (or_1_out, Game_Over, You_kinda_won);
  or or_2 (or_2_out, Length_initializer, Head_position_initializer, Initialize_direction, counter_3_carry);
  Demultiplexer #(.select(2)) demultiplexer_2 (
    .out0(M1_Clock), .out1(M2_Clock), .out2(M3_Clock), .out3(M4_Clock), .in(Main_loop), .sel(Module_num));  // open: en
  Counter #(.width(2), .max('h3), .trigger("falling")) counter_2 (
    .Q(Module_num), .clk(or_3_out));  // open: load, D, count, carry, clr
  or or_3 (or_3_out, M1, M2, M3, M4);
  Hex_Digit_Display hex_digit_display_1 (.value(Snake_length[7:4]));  // open: dp
  Hex_Digit_Display hex_digit_display_2 (.value(Snake_length[3:0]));  // open: dp
  Snake_moving_module Snake_mover (
    .Clock__in(M1_Clock), .Y_head_coordinate(Y), .X_head_coordinate(X), .X_direction(X_direction),
    .Y_direction(Y_direction), .out_9(M2), .New_Y_coordinate(Snake_mover_new_y_coordinate),
    .New_X_coordinate(Snake_mover_new_x_coordinate), .Increment_head_position_counter(Head_increment));
  LED led_1 (.in(Game_Over));
  LED led_2 (.in(Game_Over));
  LED led_3 (.in(Game_Over));
  LED led_4 (.in(Game_Over));
  LED led_5 (.in(Game_Over));
  LED led_6 (.in(Game_Over));
  Screen_output_module Display_module (
    .Snake_length__in(Snake_length), .Clock__in(M2_Clock), .End_of_a_clock_tick(M1),
    .Clock__out(Display_clock));  // open: Location_OUT
  assign M3_Address = demultiplexer_5_out0 ? Snake_head_position : 8'bz;  // Controlled_Buffer controlled_buffer_1
  Counter #(.trigger("falling")) Address (
    .Q(Address_q), .clk(demultiplexer_5_out1), .clr(comparator_2_eq));  // open: load, D, count, carry
  assign M3_Address = not_1_out ? Address_q : 8'bz;  // Controlled_Buffer controlled_buffer_2
  not not_1 (not_1_out, demultiplexer_5_out0);
  Demultiplexer #(.select(2)) demultiplexer_3 (
    .out0(demultiplexer_3_out0), .out1(demultiplexer_3_out1), .out2(demultiplexer_3_out2), .in(M4_Clock),
    .sel(Operation_counter_q));  // open: out3, en
  Counter #(.width(2), .max('h2)) Operation_counter (
    .Q(Operation_counter_q), .clk(or_4_out), .clr(demultiplexer_4_out2));  // open: load, D, count, carry
  or or_4 (or_4_out, Apple_found, M4__2);
  LED led_7 (.in(Game_Over));
  LED led_8 (.in(Game_Over));
  LED led_9 (.in(Game_Over));
  Comparator #(.mode("unsigned")) comparator_1 (.a({8{1'b0}}), .b(Snake_length), .lt(comparator_1_lt));  // open: gt, eq
  Comparator #(.mode("unsigned")) comparator_2 (
    .a(Snake_length), .b(M3_Address), .eq(comparator_2_eq));  // open: gt, lt
  and and_1 (and_1_out, not_2_out, Operation_counter_q[0]);
  not not_2 (not_2_out, Operation_counter_q[1]);
  or or_5 (or_5_out, demultiplexer_3_out2, Apple_initializer);
  LED led_10 (.in(Game_Over));
  LED led_11 (.in(Game_Over));
  LED led_12 (.in(Game_Over));
  LED led_13 (.in(Game_Over));
  LED led_14 (.in(Game_Over));
  LED led_15 (.in(Game_Over));
  LED led_16 (.in(Game_Over));
  LED led_17 (.in(Game_Over));
  LED led_18 (.in(Game_Over));
  LED led_19 (.in(Game_Over));
  Counter #(.width(3), .max('h3), .trigger("falling")) counter_3 (
    .carry(counter_3_carry), .clk(Apple_initializer), .clr(counter_3_carry));  // open: load, D, count, Q
  Hex_Digit_Display hex_digit_display_3 (.value(apple_coordinate_digit_display_1_out_3));  // open: dp
  Multiplexer #(.select(2), .width(8)) multiplexer_1 (
    .in0(Snake_head_position), .in1(Snake_head_position), .in2(M3_Address), .in3(M4_Address),
    .out(multiplexer_1_out), .sel(Module_num));  // open: en
  Multiplexer #(.select(2), .width(8)) multiplexer_2 (
    .in0(Snake_head_position), .in1(Snake_head_position), .in2(M3_Address), .in3(M4_Address),
    .out(multiplexer_2_out), .sel(Module_num));  // open: en
  Multiplexer #(.select(2), .width(5)) multiplexer_3 (
    .in0(Snake_mover_new_y_coordinate), .in3(Y__M4), .out(multiplexer_3_out), .sel(Module_num));  // open: in1, in2, en
  Multiplexer #(.select(2), .width(5)) multiplexer_4 (
    .in0(Snake_mover_new_x_coordinate), .in3(X__M4), .out(multiplexer_4_out), .sel(Module_num));  // open: in1, in2, en
  Multiplexer #(.select(2)) multiplexer_5 (
    .in0(M2), .in1(1'b0), .in2(1'b0), .in3(Memory_clock_M4), .out(multiplexer_5_out), .sel(Module_num));  // open: en
  and and_2 (M3, comparator_1_lt, comparator_2_eq);
  Multiplexer #(.width(8)) multiplexer_6 (
    .in0(Snake_head_position), .in1(Address_for_shifter), .out(M4_Address), .sel(and_1_out));  // open: en
  Demultiplexer #(.select(2)) demultiplexer_4 (
    .out0(demultiplexer_4_out0), .out1(Draw_apple), .out2(demultiplexer_4_out2), .in(or_5_out),
    .sel({counter_4_q[1], Apple_coordinates}));  // open: out3, en
  Counter #(.width(2), .max('h2), .trigger("falling")) counter_4 (
    .Q({counter_4_q[1], Apple_coordinates}), .clk(or_5_out));  // open: load, D, count, carry, clr
  LED led_20 (.in(Game_Over));
  LED led_21 (.in(Game_Over));
  LED led_22 (.in(Game_Over));
  LED led_23 (.in(Game_Over));
  LED led_24 (.in(Game_Over));
  LED led_25 (.in(Game_Over));
  LED led_26 (.in(Game_Over));
  LED led_27 (.in(Game_Over));
  LED led_28 (.in(Game_Over));
  Hex_Digit_Display hex_digit_display_4 (.value(apple_coordinate_digit_display_1_out_4));  // open: dp
  Hex_Digit_Display hex_digit_display_5 (.value(apple_coordinate_digit_display_1_out_5));  // open: dp
  Apple_coordinate_digit_display apple_coordinate_digit_display_1 (
    .in_1(Apple_X), .in_2(Apple_Y), .out_3(apple_coordinate_digit_display_1_out_3),
    .out_4(apple_coordinate_digit_display_1_out_4), .out_5(apple_coordinate_digit_display_1_out_5),
    .out_6(apple_coordinate_digit_display_1_out_6));
  Register #(.width(5), .trigger("high")) Head_position_X (
    .D(X), .Q(Head_position_X_q), .clk(demultiplexer_3_out0));  // open: en, clr
  Register #(.width(5), .trigger("high")) Head_position_Y (
    .D(Y), .Q(Head_position_Y_q), .clk(demultiplexer_3_out0));  // open: en, clr
  Random #(.width(5)) random_1 (.clk(demultiplexer_4_out0), .out(Apple_X));  // open: next, clr
  Random #(.width(5), .seed(1)) random_2 (.clk(demultiplexer_4_out0), .out(Apple_Y));  // open: next, clr
  Adder adder_1 (.a(Snake_head_position), .b(8'h1), .out(adder_1_out));  // open: cin, cout
  LED led_29 (.in(Game_Over));
  LED led_30 (.in(Game_Over));
  LED led_31 (.in(Game_Over));
  LED led_32 (.in(Game_Over));
  LED led_33 (.in(Game_Over));
  Hex_Digit_Display hex_digit_display_6 (.value(apple_coordinate_digit_display_1_out_6));  // open: dp
  RAM #(.dataWidth(5), .bus("separate")) ram_1 (
    .addr(multiplexer_1_out), .din(multiplexer_3_out), .data(Y), .clk(multiplexer_5_out));  // open: str, sel, ld, clr
  RAM #(.dataWidth(5), .bus("separate")) ram_2 (
    .addr(multiplexer_2_out), .din(multiplexer_4_out), .data(X), .clk(multiplexer_5_out));  // open: str, sel, ld, clr
  Demultiplexer demultiplexer_5 (
    .out0(demultiplexer_5_out0), .out1(demultiplexer_5_out1), .in(M3_Clock), .sel(Operation_counter_2_q));  // open: en
  Counter #(.width(1), .max('h1), .trigger("falling")) Operation_counter_2 (
    .Q(Operation_counter_2_q), .clk(demultiplexer_5_out0), .clr(comparator_2_eq));  // open: load, D, count, carry
  Comparator #(.mode("unsigned")) comparator_3 (
    .a(Snake_head_position), .b(M3_Address), .eq(comparator_3_eq));  // open: gt, lt
  LED led_34 (.in(Game_Over));
  LED led_35 (.in(Game_Over));
  LED led_36 (.in(Game_Over));
  LED led_37 (.in(Game_Over));
  LED led_38 (.in(Game_Over));
  LED led_39 (.in(Game_Over));
  LED led_40 (.in(Game_Over));
  LED led_41 (.in(Game_Over));
  Keyboard keyboard_1 (.clr(Input_controller_reset_keyboard), .data(keyboard_1_data));  // open: clk, re, avail
  Button A (.out(A_out));
  not not_3 (not_3_out, Apple_coordinates);
  assign controlled_buffer_3_out = not_3_out ? Y : 5'bz;  // Controlled_Buffer controlled_buffer_3
  assign controlled_buffer_4_out = not_3_out ? X : 5'bz;  // Controlled_Buffer controlled_buffer_4
  Comparator #(.width(5), .mode("unsigned")) comparator_4 (
    .a(Head_position_X_q), .b(Apple_X), .eq(comparator_4_eq));  // open: gt, lt
  Comparator #(.width(5), .mode("unsigned")) comparator_5 (
    .a(Apple_Y), .b(Head_position_Y_q), .eq(comparator_5_eq));  // open: gt, lt
  Snake_grow_module Memory_shifter (
    .Snake_length(Snake_length), .Starting_position(adder_1_out), .X(X), .Y(Y), .Clock(demultiplexer_3_out1),
    .Memory_clock_out(Memory_clock_M4), .Done(M4__2), .Address__out(Address_for_shifter), .X__out(X__M4),
    .Y__out(Y__M4));
  LED led_42 (.in(You_kinda_won));
  LED led_43 (.in(You_kinda_won));
  LED led_44 (.in(You_kinda_won));
  LED led_45 (.in(You_kinda_won));
  Button W (.out(W_out));
  Button D (.out(D_out));
  Button S (.out(S_out));
  assign controlled_buffer_3_out = Apple_coordinates ? Apple_Y : 5'bz;  // Controlled_Buffer controlled_buffer_5
  assign controlled_buffer_4_out = Apple_coordinates ? Apple_X : 5'bz;  // Controlled_Buffer controlled_buffer_6
  Register #(.width(5), .trigger("high")) register_1 (
    .D(controlled_buffer_4_out), .Q(register_1_q), .clk(Head_increment));  // open: en, clr
  Register #(.width(5), .trigger("high")) register_2 (
    .D(controlled_buffer_3_out), .Q(register_2_q), .clk(Head_increment));  // open: en, clr
  Register #(.width(5), .trigger("high")) Head_position_X_2 (
    .D(X), .Q(Head_position_X_2_q), .clk(demultiplexer_5_out0));  // open: en, clr
  Register #(.width(5), .trigger("high")) Head_position_Y_2 (
    .D(Y), .Q(Head_position_Y_2_q), .clk(demultiplexer_5_out0));  // open: en, clr
  and and_3 (and_3_out, comparator_4_eq, comparator_5_eq);
  and and_4 (and_4_out, demultiplexer_3_out0, and_3_out);
  LED led_46 (.in(You_kinda_won));
  LED led_47 (.in(You_kinda_won));
  LED led_48 (.in(You_kinda_won));
  LED led_49 (.in(You_kinda_won));
  Key_control_module Input_controller (
    .D(D_out), .A(A_out), .S(S_out), .W(W_out), .Keyboard(keyboard_1_data),
    .Reset_keyboard(Input_controller_reset_keyboard), .in_3(Initialize_direction), .X_direction(X_direction),
    .Y_direction(Y_direction));
  Counter #(.width(1), .max('h1)) counter_5 (
    .D(and_3_out), .Q(Increment_snake_s_length), .clk(and_3_out), .clr(Increment_snake_s_length));  // open: load, count, carry
  Counter #(.width(1), .max('h1), .trigger("falling")) counter_6 (
    .Q(counter_6_q), .clk(demultiplexer_3_out0));  // open: load, D, count, carry, clr
  Counter #(.width(1), .max('h1), .trigger("falling")) counter_7 (
    .Q(Apple_found), .clk(and_4_out), .clr(Apple_found));  // open: load, D, count, carry
  LED led_50 (.in(You_kinda_won));
  LED led_51 (.in(You_kinda_won));
  LED led_52 (.in(You_kinda_won));
  LED led_53 (.in(You_kinda_won));
  LED led_54 (.in(You_kinda_won));
  LED led_55 (.in(You_kinda_won));
  DotMatrix #(.matrixcols(32), .matrixrows(32)) dotmatrix_1 (
    .col0(display_curcuit_32_bits_1_out_7), .col1(display_curcuit_32_bits_1_out_8),
    .col2(display_curcuit_32_bits_1_out_9), .col3(display_curcuit_32_bits_1_out_10),
    .col4(display_curcuit_32_bits_1_out_11), .col5(display_curcuit_32_bits_1_out_12),
    .col6(display_curcuit_32_bits_1_out_13), .col7(display_curcuit_32_bits_1_out_14),
    .col8(display_curcuit_32_bits_1_out_15), .col9(display_curcuit_32_bits_1_out_16),
    .col10(display_curcuit_32_bits_1_out_17), .col11(display_curcuit_32_bits_1_out_18),
    .col12(display_curcuit_32_bits_1_out_19), .col13(display_curcuit_32_bits_1_out_20),
    .col14(display_curcuit_32_bits_1_out_21), .col15(display_curcuit_32_bits_1_out_22),
    .col16(display_curcuit_32_bits_1_out_23), .col17(display_curcuit_32_bits_1_out_24),
    .col18(display_curcuit_32_bits_1_out_25), .col19(display_curcuit_32_bits_1_out_26),
    .col20(display_curcuit_32_bits_1_out_27), .col21(display_curcuit_32_bits_1_out_28),
    .col22(display_curcuit_32_bits_1_out_29), .col23(display_curcuit_32_bits_1_out_30),
    .col24(display_curcuit_32_bits_1_out_31), .col25(display_curcuit_32_bits_1_out_32),
    .col26(display_curcuit_32_bits_1_out_33), .col27(display_curcuit_32_bits_1_out_34),
    .col28(display_curcuit_32_bits_1_out_35), .col29(display_curcuit_32_bits_1_out_36),
    .col30(display_curcuit_32_bits_1_out_37), .col31(display_curcuit_32_bits_1_out_38));
  Display_curcuit__32_bits display_curcuit_32_bits_1 (
    .Clock(or_6_out), .Y_positions(controlled_buffer_3_out), .X_positions(controlled_buffer_4_out),
    .Reset_column_num(register_1_q), .Reset_row_num(register_2_q), .Reset__x_y(M2),
    .out_7(display_curcuit_32_bits_1_out_7), .out_8(display_curcuit_32_bits_1_out_8),
    .out_9(display_curcuit_32_bits_1_out_9), .out_10(display_curcuit_32_bits_1_out_10),
    .out_11(display_curcuit_32_bits_1_out_11), .out_12(display_curcuit_32_bits_1_out_12),
    .out_13(display_curcuit_32_bits_1_out_13), .out_14(display_curcuit_32_bits_1_out_14),
    .out_15(display_curcuit_32_bits_1_out_15), .out_16(display_curcuit_32_bits_1_out_16),
    .out_17(display_curcuit_32_bits_1_out_17), .out_18(display_curcuit_32_bits_1_out_18),
    .out_19(display_curcuit_32_bits_1_out_19), .out_20(display_curcuit_32_bits_1_out_20),
    .out_21(display_curcuit_32_bits_1_out_21), .out_22(display_curcuit_32_bits_1_out_22),
    .out_23(display_curcuit_32_bits_1_out_23), .out_24(display_curcuit_32_bits_1_out_24),
    .out_25(display_curcuit_32_bits_1_out_25), .out_26(display_curcuit_32_bits_1_out_26),
    .out_27(display_curcuit_32_bits_1_out_27), .out_28(display_curcuit_32_bits_1_out_28),
    .out_29(display_curcuit_32_bits_1_out_29), .out_30(display_curcuit_32_bits_1_out_30),
    .out_31(display_curcuit_32_bits_1_out_31), .out_32(display_curcuit_32_bits_1_out_32),
    .out_33(display_curcuit_32_bits_1_out_33), .out_34(display_curcuit_32_bits_1_out_34),
    .out_35(display_curcuit_32_bits_1_out_35), .out_36(display_curcuit_32_bits_1_out_36),
    .out_37(display_curcuit_32_bits_1_out_37), .out_38(display_curcuit_32_bits_1_out_38));
  Comparator #(.width(5), .mode("unsigned")) comparator_6 (
    .a(Head_position_X_2_q), .b(X), .eq(comparator_6_eq));  // open: gt, lt
  Comparator #(.width(5), .mode("unsigned")) comparator_7 (
    .a(Y), .b(Head_position_Y_2_q), .eq(comparator_7_eq));  // open: gt, lt
  and and_5 (and_5_out, counter_6_q, demultiplexer_3_out0);
  LED led_56 (.in(You_kinda_won));
  LED led_57 (.in(You_kinda_won));
  LED led_58 (.in(You_kinda_won));
  LED led_59 (.in(You_kinda_won));
  LED led_60 (.in(You_kinda_won));
  LED led_61 (.in(You_kinda_won));
  LED led_62 (.in(You_kinda_won));
  LED led_63 (.in(You_kinda_won));
  and and_6 (and_6_out, comparator_6_eq, comparator_7_eq);
  Snake_head_position_counter__rising_edge Head_position (
    .Snake_length__in(Snake_length), .Initialize_with_data(Head_position_initializer),
    .Increment(Head_increment), .Head_location_out(Snake_head_position));  // open: Looped
  LED led_64 (.in(You_kinda_won));
  LED led_65 (.in(You_kinda_won));
  LED led_66 (.in(You_kinda_won));
  LED led_67 (.in(You_kinda_won));
  LED led_68 (.in(You_kinda_won));
  LED led_69 (.in(You_kinda_won));
  LED led_70 (.in(You_kinda_won));
  LED led_71 (.in(You_kinda_won));
  LED led_72 (.in(You_kinda_won));
  LED led_73 (.in(You_kinda_won));
  LED led_74 (.in(You_kinda_won));
  or or_6 (or_6_out, Draw_apple, Display_clock);
  and and_7 (and_7_out, and_6_out, demultiplexer_5_out1, ~comparator_3_eq);  // AND_Gate
  or or_7 (M4, and_5_out, M4__2);
  Comparator #(.mode("unsigned")) comparator_8 (.a(Snake_length), .b(8'h32), .gt(You_kinda_won));  // open: eq, lt
  LED led_75 (.in(You_kinda_won));
  LED led_76 (.in(You_kinda_won));
  LED led_77 (.in(You_kinda_won));
  LED led_78 (.in(You_kinda_won));
  LED led_79 (.in(You_kinda_won));
  LED led_80 (.in(You_kinda_won));
  LED led_81 (.in(You_kinda_won));
  LED led_82 (.in(You_kinda_won));
  LED led_83 (.in(You_kinda_won));
  LED led_84 (.in(You_kinda_won));
  LED led_85 (.in(You_kinda_won));
  D_Flip_Flop d_ff_1 (.clk(and_7_out), .D(and_7_out), .Q(Game_Over));  // open: Qn, preset, en, reset
  Snake_length_counter u_Snake_length (
    .Initialize(Length_initializer), .Increment_snake_length(Increment_snake_s_length),
    .Snake_Length_OUT(Snake_length));

  // Other names for the same wires on the sheet: reset__x__y = M2

  // Notes on the sheet:
  //   To start, press CTRL+K
  //   To restart, press CTRL+R
  //   By Dmitrii Korobeinikov
  //   Done
  //   Create new apple
  //   snake shifting (for snake's grow!)
  //   Keyboard. Poke it and use a real one
  //   Curcuit that determines if snake is iting eatself
endmodule

module ORer__8_bits (
  input  [7:0] in_1,
  input  [7:0] in_2,
  output [7:0] out_3
);

  or or_1 (out_3[0], in_1[0], in_2[0]);
  or or_2 (out_3[1], in_1[1], in_2[1]);
  or or_3 (out_3[2], in_1[2], in_2[2]);
  or or_4 (out_3[3], in_1[3], in_2[3]);
  or or_5 (out_3[4], in_1[4], in_2[4]);
  or or_6 (out_3[5], in_1[5], in_2[5]);
  or or_7 (out_3[6], in_1[6], in_2[6]);
  or or_8 (out_3[7], in_1[7], in_2[7]);
endmodule

module ORer__4_bits (
  input  [3:0] in_1,
  input  [3:0] in_2,
  output [3:0] out_3
);

  or or_1 (out_3[0], in_1[0], in_2[0]);
  or or_2 (out_3[1], in_1[1], in_2[1]);
  or or_3 (out_3[2], in_1[2], in_2[2]);
  or or_4 (out_3[3], in_1[3], in_2[3]);
endmodule

module ORed_Register (
  input  [31:0] Data_to_write,
  input  Clock,
  input  [4:0] Row__to_null,
  input  Reset_a_row_num,
  output [31:0] out_5
);

  wire not_1_out, or_1_out;
  wire [31:0] ander_32_bits_1_out_3, controlled_buffer_1_out, not_2_out, orer_32_bits_1_out_3, shifter_1_out;

  assign controlled_buffer_1_out = not_1_out ? orer_32_bits_1_out_3 : 32'bz;  // Controlled_Buffer controlled_buffer_1
  ORer__32_bits orer_32_bits_1 (.in_1(Data_to_write), .in_2(out_5), .out_3(orer_32_bits_1_out_3));
  not not_1 (not_1_out, Reset_a_row_num);
  or or_1 (or_1_out, Reset_a_row_num, Clock);
  Register #(.width(32), .trigger("high")) register_1 (
    .D(controlled_buffer_1_out), .Q(out_5), .clk(or_1_out));  // open: en, clr
  Shifter #(.width(32)) shifter_1 (.in(32'h1), .\dist (Row__to_null), .out(shifter_1_out));
  ANDer__32_bits ander_32_bits_1 (.in_1(out_5), .in_2(not_2_out), .out_3(ander_32_bits_1_out_3));
  assign not_2_out = ~shifter_1_out;  // NOT_Gate not_2, 32 bits wide
  assign controlled_buffer_1_out = Reset_a_row_num ? ander_32_bits_1_out_3 : 32'bz;  // Controlled_Buffer controlled_buffer_2

  // Notes on the sheet:
  //   When a value is inputted, it is ORed onto the register. That is, input value can
  //   only make a bit 1
endmodule

module Display_unit_curcuit (
  input  [4:0] Y_Position,
  input  [1:0] X_position,
  input  Clock,
  input  [1:0] Reset_column_num,
  input  [4:0] reset_row_num,
  input  Reset__x__y,
  output [31:0] Screen_OUT,
  output [31:0] Screen_OUT_2,
  output [31:0] Screen_OUT_3,
  output [31:0] Screen_OUT_4
);

  wire demultiplexer_2_out0, demultiplexer_2_out1, demultiplexer_2_out2, demultiplexer_2_out3,
       demultiplexer_3_out0, demultiplexer_3_out1, demultiplexer_3_out2, demultiplexer_3_out3;
  wire [31:0] demultiplexer_1_out0, demultiplexer_1_out1, demultiplexer_1_out2, demultiplexer_1_out3,
       shifter_1_out;

  Demultiplexer #(.select(2), .width(32)) demultiplexer_1 (
    .out0(demultiplexer_1_out0), .out1(demultiplexer_1_out1), .out2(demultiplexer_1_out2),
    .out3(demultiplexer_1_out3), .in(shifter_1_out), .sel(X_position));  // open: en
  Shifter #(.width(32)) shifter_1 (.in(32'h1), .\dist (Y_Position), .out(shifter_1_out));
  Demultiplexer #(.select(2)) demultiplexer_2 (
    .out0(demultiplexer_2_out0), .out1(demultiplexer_2_out1), .out2(demultiplexer_2_out2),
    .out3(demultiplexer_2_out3), .in(Clock), .sel(X_position));  // open: en
  ORed_Register ored_register_1 (
    .Data_to_write(demultiplexer_1_out0), .Clock(demultiplexer_2_out0), .Row__to_null(reset_row_num),
    .Reset_a_row_num(demultiplexer_3_out0), .out_5(Screen_OUT));
  ORed_Register ored_register_2 (
    .Data_to_write(demultiplexer_1_out1), .Clock(demultiplexer_2_out1), .Row__to_null(reset_row_num),
    .Reset_a_row_num(demultiplexer_3_out1), .out_5(Screen_OUT_2));
  ORed_Register ored_register_3 (
    .Data_to_write(demultiplexer_1_out2), .Clock(demultiplexer_2_out2), .Row__to_null(reset_row_num),
    .Reset_a_row_num(demultiplexer_3_out2), .out_5(Screen_OUT_3));
  ORed_Register ored_register_4 (
    .Data_to_write(demultiplexer_1_out3), .Clock(demultiplexer_2_out3), .Row__to_null(reset_row_num),
    .Reset_a_row_num(demultiplexer_3_out3), .out_5(Screen_OUT_4));
  Demultiplexer #(.select(2)) demultiplexer_3 (
    .out0(demultiplexer_3_out0), .out1(demultiplexer_3_out1), .out2(demultiplexer_3_out2),
    .out3(demultiplexer_3_out3), .in(Reset__x__y), .sel(Reset_column_num));  // open: en

  // Notes on the sheet:
  //   Memory in
  //   Memory in
  //   Output to screen
endmodule

module Display_curcuit__8_bits (
  input  [4:0] Y_Positions,
  input  [2:0] X_Positions,
  input  Clock,
  input  [2:0] Reset_column_num,
  input  [4:0] Reset_row_num,
  input  Reset__x__y,
  output [31:0] Screen_OUT,
  output [31:0] Screen_OUT_2,
  output [31:0] Screen_OUT_3,
  output [31:0] Screen_OUT_4,
  output [31:0] Screen_OUT_5,
  output [31:0] Screen_OUT_6,
  output [31:0] Screen_OUT_7,
  output [31:0] Screen_OUT_8
);

  wire demultiplexer_1_out0, demultiplexer_1_out1, demultiplexer_2_out0, demultiplexer_2_out1;

  Demultiplexer demultiplexer_1 (
    .out0(demultiplexer_1_out0), .out1(demultiplexer_1_out1), .in(Clock), .sel(X_Positions[2]));  // open: en
  Display_unit_curcuit display_unit_curcuit_1 (
    .Y_Position(Y_Positions), .X_position(X_Positions[1:0]), .Clock(demultiplexer_1_out0),
    .Reset_column_num(Reset_column_num[1:0]), .reset_row_num(Reset_row_num),
    .Reset__x__y(demultiplexer_2_out0), .Screen_OUT(Screen_OUT), .Screen_OUT_2(Screen_OUT_2),
    .Screen_OUT_3(Screen_OUT_3), .Screen_OUT_4(Screen_OUT_4));
  Display_unit_curcuit display_unit_curcuit_2 (
    .Y_Position(Y_Positions), .X_position(X_Positions[1:0]), .Clock(demultiplexer_1_out1),
    .Reset_column_num(Reset_column_num[1:0]), .reset_row_num(Reset_row_num),
    .Reset__x__y(demultiplexer_2_out1), .Screen_OUT(Screen_OUT_5), .Screen_OUT_2(Screen_OUT_6),
    .Screen_OUT_3(Screen_OUT_7), .Screen_OUT_4(Screen_OUT_8));
  Demultiplexer demultiplexer_2 (
    .out0(demultiplexer_2_out0), .out1(demultiplexer_2_out1), .in(Reset__x__y), .sel(Reset_column_num[2]));  // open: en
endmodule

module Memory_Shifter (
  input  [3:0] Snake_length,
  input  [3:0] Starting_position,
  input  [2:0] Data__in,
  input  Clock,
  output [3:0] Address__out,
  output [2:0] Data__out,
  output Memory_clock_out,
  output Done
);

  wire and_1_out, comparator_1_eq;
  wire [3:0] counter_1_q;

  Counter #(.width(4), .max('hf), .trigger("falling")) counter_1 (
    .Q(counter_1_q), .clk(Clock), .clr(Done));  // open: load, D, count, carry
  Adder #(.width(4)) adder_1 (.a(Starting_position), .b(counter_1_q), .out(Address__out));  // open: cin, cout
  Comparator #(.width(4)) comparator_1 (.a(Snake_length), .b(Address__out), .eq(comparator_1_eq));  // open: gt, lt
  Register #(.width(3)) register_1 (.D(Data__in), .Q(Data__out), .clk(Clock));  // open: en, clr
  and and_1 (and_1_out, comparator_1_eq, Clock);
  Counter #(.width(1), .max('h1), .trigger("falling")) counter_2 (
    .Q(Done), .clk(and_1_out), .clr(Done));  // open: load, D, count, carry

  assign Memory_clock_out = Clock;
endmodule

module ORer__3_bits (
  input  [2:0] in_1,
  input  [2:0] in_2,
  output [2:0] out_3
);

  or or_1 (out_3[0], in_1[0], in_2[0]);
  or or_2 (out_3[1], in_1[1], in_2[1]);
  or or_3 (out_3[2], in_1[2], in_2[2]);
endmodule

module OR_gate___3_bits (
  input  [2:0] in_1,
  output out_2
);

  or or_1 (out_2, in_1[0], in_1[1], in_1[2]);
endmodule

module Limited_counter__falling_edge (
  input  [7:0] Snake_length,
  input  Increment,
  output [7:0] Location_OUT,
  output Looped
);

  Counter #(.trigger("falling")) counter_1 (
    .Q(Location_OUT), .clk(Increment), .clr(Looped));  // open: load, D, count, carry
  Comparator #(.mode("unsigned")) comparator_1 (.a(Snake_length), .b(Location_OUT), .eq(Looped));  // open: gt, lt
endmodule

module Snake_length_counter (
  input  Initialize,
  input  Increment_snake_length,
  output [7:0] Snake_Length_OUT
);

  wire not_1_out, or_1_out;

  not not_1 (not_1_out, Initialize);
  or or_1 (or_1_out, Initialize, Increment_snake_length);
  Counter Snake_length (
    .load(Initialize), .D(8'h2), .count(not_1_out), .Q(Snake_Length_OUT), .clk(or_1_out));  // open: carry, clr
endmodule

module Screen_output_module (
  input  [7:0] Snake_length__in,
  input  Clock__in,
  output [7:0] Location_OUT,
  output Clock__out,
  output End_of_a_clock_tick
);

  Limited_counter__falling_edge limited_counter_falling_edge_1 (
    .Snake_length(Snake_length__in), .Increment(Clock__in), .Location_OUT(Location_OUT));  // open: Looped
  Counter #(.width(1), .max('h1), .trigger("falling")) counter_1 (
    .Q(End_of_a_clock_tick), .clk(Clock__in), .clr(End_of_a_clock_tick));  // open: load, D, count, carry

  assign Clock__out = Clock__in;
endmodule

module Snake_head_position_counter__rising_edge (
  input  [7:0] Snake_length__in,
  input  Initialize_with_data,
  input  Increment,
  output [7:0] Head_location_out,
  output Looped
);

  wire not_1_out, or_1_out;
  wire [7:0] subtractor_1_out;

  Subtractor subtractor_1 (.a(Snake_length__in), .b(8'h1), .out(subtractor_1_out));  // open: bin, bout
  Counter counter_1 (
    .load(Initialize_with_data), .D(subtractor_1_out), .count(not_1_out), .Q(Head_location_out),
    .clk(or_1_out), .clr(Looped));  // open: carry
  not not_1 (not_1_out, Initialize_with_data);
  or or_1 (or_1_out, Initialize_with_data, Increment);
  Comparator #(.mode("unsigned")) comparator_1 (
    .a(Snake_length__in), .b(Head_location_out), .eq(Looped));  // open: gt, lt
endmodule

module Snake_moving_module (
  input  Clock__in,
  input  [4:0] Y_head_coordinate,
  input  [4:0] X_head_coordinate,
  input  [4:0] X_direction,
  input  [4:0] Y_direction,
  output [4:0] New_Y_coordinate,
  output [4:0] New_X_coordinate,
  output Increment_head_position_counter,
  output out_9
);

  wire [4:0] X_head_position_q, Y_head_position_q;

  Register #(.width(5)) X_head_position (
    .D(X_head_coordinate), .Q(X_head_position_q), .clk(Clock__in));  // open: en, clr
  Adder #(.width(5)) adder_1 (.a(X_head_position_q), .b(X_direction), .out(New_X_coordinate));  // open: cin, cout
  Register #(.width(5)) Y_head_position (
    .D(Y_head_coordinate), .Q(Y_head_position_q), .clk(Clock__in));  // open: en, clr
  Adder #(.width(5)) adder_2 (.a(Y_head_position_q), .b(Y_direction), .out(New_Y_coordinate));  // open: cin, cout
  Counter #(.width(1), .max('h1), .trigger("falling")) counter_1 (
    .Q(out_9), .clk(Clock__in), .clr(out_9));  // open: load, D, count, carry

  assign Increment_head_position_counter = Clock__in;
endmodule

module Key_control_module (
  input  [6:0] Keyboard,
  input  D,
  input  in_3,
  input  A,
  input  S,
  input  W,
  output Reset_keyboard,
  output [4:0] X_direction,
  output [4:0] Y_direction
);

  wire and_1_out, and_2_out, comparator_1_eq, comparator_2_eq, comparator_3_eq, comparator_4_eq,
       comparator_5_eq, comparator_6_eq, or_1_out, or_3_out, or_4_out, or_5_out, or_6_out, or_9_out,
       or_10_out, X_direction_accepted, Y_direction_accepted;
  wire [4:0] multiplexer_1_out, multiplexer_2_out;

  or or_1 (or_1_out, in_3, D);
  or or_2 (Reset_keyboard, Y_direction_accepted, X_direction_accepted);
  Comparator #(.width(7)) comparator_1 (.a(Keyboard), .b(7'b1100001), .eq(comparator_1_eq));  // open: gt, lt
  Comparator #(.width(7)) comparator_2 (.a(Keyboard), .b(7'b1100100), .eq(comparator_2_eq));  // open: gt, lt
  Comparator #(.width(7)) comparator_3 (.a(Keyboard), .b(7'b1110111), .eq(comparator_3_eq));  // open: gt, lt
  Comparator #(.width(7)) comparator_4 (.a(Keyboard), .b(7'b1110011), .eq(comparator_4_eq));  // open: gt, lt
  or or_3 (or_3_out, comparator_1_eq, A);
  or or_4 (or_4_out, or_1_out, comparator_2_eq);
  or or_5 (or_5_out, comparator_3_eq, W);
  or or_6 (or_6_out, S, comparator_4_eq);
  or or_7 (Y_direction_accepted, or_3_out, or_4_out);
  or or_8 (X_direction_accepted, or_6_out, or_5_out);
  Multiplexer #(.width(5)) multiplexer_1 (
    .in0({5{1'b1}}), .in1(5'b00001), .out(multiplexer_1_out), .sel(or_4_out));  // open: en
  or or_9 (or_9_out, or_4_out, or_3_out);
  Comparator #(.width(5), .mode("unsigned")) comparator_5 (
    .a(X_direction), .b({5{1'b0}}), .eq(comparator_5_eq));  // open: gt, lt
  Comparator #(.width(5), .mode("unsigned")) comparator_6 (
    .a({5{1'b0}}), .b(Y_direction), .eq(comparator_6_eq));  // open: gt, lt
  Multiplexer #(.width(5)) multiplexer_2 (
    .in0(5'b00001), .in1({5{1'b1}}), .out(multiplexer_2_out), .sel(or_6_out));  // open: en
  or or_10 (or_10_out, or_6_out, or_5_out);
  Register #(.width(5), .trigger("falling")) register_1 (
    .D(multiplexer_1_out), .Q(X_direction), .clk(and_1_out), .clr(and_2_out));  // open: en
  and and_1 (and_1_out, or_9_out, comparator_5_eq);
  Register #(.width(5), .trigger("falling")) register_2 (
    .D(multiplexer_2_out), .Q(Y_direction), .clk(and_2_out), .clr(and_1_out));  // open: en
  and and_2 (and_2_out, comparator_6_eq, or_10_out);
endmodule

module Initialized_register__rising_edge (
  input  [2:0] Initializing_value,
  input  Initialize,
  input  [2:0] Data__value_stored_on_clock_trigger,
  input  Clear__when_1__pin_value_to_0_asynchronously,
  input  Clock__value_updates_on_trigger,
  output [2:0] Output__register_s_current_value
);

  wire or_1_out;
  wire [2:0] controlled_buffer_1_out;

  assign controlled_buffer_1_out = Clock__value_updates_on_trigger ? Data__value_stored_on_clock_trigger : 3'bz;  // Controlled_Buffer controlled_buffer_1
  assign controlled_buffer_1_out = Initialize ? Initializing_value : 3'bz;  // Controlled_Buffer controlled_buffer_2
  Register #(.width(3)) register_1 (
    .D(controlled_buffer_1_out), .Q(Output__register_s_current_value), .clk(or_1_out),
    .clr(Clear__when_1__pin_value_to_0_asynchronously));  // open: en
  or or_1 (or_1_out, Initialize, Clock__value_updates_on_trigger);
endmodule

module Inhibiting_counter__1_16 (
  input  Clock__in,
  output Clock_out
);

  Counter #(.width(4), .max('hf)) counter_1 (.carry(Clock_out), .clk(Clock__in));  // open: load, D, count, Q, clr
endmodule

module ANDer__8_bits (
  input  [7:0] in_1,
  input  [7:0] in_2,
  output [7:0] out_3
);

  and and_1 (out_3[0], in_1[0], in_2[0]);
  and and_2 (out_3[1], in_1[1], in_2[1]);
  and and_3 (out_3[2], in_1[2], in_2[2]);
  and and_4 (out_3[3], in_1[3], in_2[3]);
  and and_5 (out_3[4], in_1[4], in_2[4]);
  and and_6 (out_3[5], in_1[5], in_2[5]);
  and and_7 (out_3[6], in_1[6], in_2[6]);
  and and_8 (out_3[7], in_1[7], in_2[7]);
endmodule

module Snake_grow_module (
  input  [7:0] Snake_length,
  input  [7:0] Starting_position,
  input  [4:0] X,
  input  [4:0] Y,
  input  Clock,
  output Memory_clock_out,
  output [7:0] Address__out,
  output [4:0] X__out,
  output [4:0] Y__out,
  output Done
);

  Memory_Shifter__32_bits memory_shifter_32_bits_1 (
    .Snake_length(Snake_length), .Starting_position(Starting_position), .Data__in(X), .Clock(Clock),
    .Memory_clock_out(Memory_clock_out), .Address__out(Address__out), .Data__out(X__out));  // open: Done
  Memory_Shifter__32_bits memory_shifter_32_bits_2 (
    .Snake_length(Snake_length), .Starting_position(Starting_position), .Data__in(Y), .Clock(Clock),
    .Done(Done), .Data__out(Y__out));  // open: Memory_clock_out, Address__out
endmodule

module ORer__32_bits (
  input  [31:0] in_1,
  input  [31:0] in_2,
  output [31:0] out_3
);

  ORer__8_bits orer_8_bits_1 (.in_1(in_1[7:0]), .in_2(in_2[7:0]), .out_3(out_3[7:0]));
  ORer__8_bits orer_8_bits_2 (.in_1(in_1[15:8]), .in_2(in_2[15:8]), .out_3(out_3[15:8]));
  ORer__8_bits orer_8_bits_3 (.in_1(in_1[23:16]), .in_2(in_2[23:16]), .out_3(out_3[23:16]));
  ORer__8_bits orer_8_bits_4 (.in_1(in_1[31:24]), .in_2(in_2[31:24]), .out_3(out_3[31:24]));
endmodule

module ANDer__32_bits (
  input  [31:0] in_1,
  input  [31:0] in_2,
  output [31:0] out_3
);

  ANDer__8_bits ander_8_bits_1 (.in_1(in_1[7:0]), .in_2(in_2[7:0]), .out_3(out_3[7:0]));
  ANDer__8_bits ander_8_bits_2 (.in_1(in_1[15:8]), .in_2(in_2[15:8]), .out_3(out_3[15:8]));
  ANDer__8_bits ander_8_bits_3 (.in_1(in_1[23:16]), .in_2(in_2[23:16]), .out_3(out_3[23:16]));
  ANDer__8_bits ander_8_bits_4 (.in_1(in_1[31:24]), .in_2(in_2[31:24]), .out_3(out_3[31:24]));
endmodule

module Memory_Shifter__32_bits (
  input  [7:0] Snake_length,
  input  [7:0] Starting_position,
  input  [4:0] Data__in,
  input  Clock,
  output [7:0] Address__out,
  output [4:0] Data__out,
  output Memory_clock_out,
  output Done
);

  wire and_1_out, comparator_1_eq;
  wire [7:0] counter_1_q;

  Counter #(.trigger("falling")) counter_1 (.Q(counter_1_q), .clk(Clock), .clr(Done));  // open: load, D, count, carry
  Adder adder_1 (.a(Starting_position), .b(counter_1_q), .out(Address__out));  // open: cin, cout
  Comparator #(.mode("unsigned")) comparator_1 (
    .a(Snake_length), .b(Address__out), .eq(comparator_1_eq));  // open: gt, lt
  Register #(.width(5)) register_1 (.D(Data__in), .Q(Data__out), .clk(Clock));  // open: en, clr
  and and_1 (and_1_out, comparator_1_eq, Clock);
  Counter #(.width(1), .max('h1), .trigger("falling")) counter_2 (
    .Q(Done), .clk(and_1_out), .clr(Done));  // open: load, D, count, carry

  assign Memory_clock_out = Clock;
endmodule

module Display_curcuit__32_bits (
  input  Clock,
  input  [4:0] Y_positions,
  input  [4:0] X_positions,
  input  [4:0] Reset_column_num,
  input  [4:0] Reset_row_num,
  input  Reset__x_y,
  output [31:0] out_7,
  output [31:0] out_8,
  output [31:0] out_9,
  output [31:0] out_10,
  output [31:0] out_11,
  output [31:0] out_12,
  output [31:0] out_13,
  output [31:0] out_14,
  output [31:0] out_15,
  output [31:0] out_16,
  output [31:0] out_17,
  output [31:0] out_18,
  output [31:0] out_19,
  output [31:0] out_20,
  output [31:0] out_21,
  output [31:0] out_22,
  output [31:0] out_23,
  output [31:0] out_24,
  output [31:0] out_25,
  output [31:0] out_26,
  output [31:0] out_27,
  output [31:0] out_28,
  output [31:0] out_29,
  output [31:0] out_30,
  output [31:0] out_31,
  output [31:0] out_32,
  output [31:0] out_33,
  output [31:0] out_34,
  output [31:0] out_35,
  output [31:0] out_36,
  output [31:0] out_37,
  output [31:0] out_38
);

  wire demultiplexer_1_out0, demultiplexer_1_out1, demultiplexer_1_out2, demultiplexer_1_out3,
       demultiplexer_2_out0, demultiplexer_2_out1, demultiplexer_2_out2, demultiplexer_2_out3;

  Demultiplexer #(.select(2)) demultiplexer_1 (
    .out0(demultiplexer_1_out0), .out1(demultiplexer_1_out1), .out2(demultiplexer_1_out2),
    .out3(demultiplexer_1_out3), .in(Clock), .sel(X_positions[4:3]));  // open: en
  Display_curcuit__8_bits display_curcuit_8_bits_1 (
    .Y_Positions(Y_positions), .X_Positions(X_positions[2:0]), .Clock(demultiplexer_1_out0),
    .Reset_column_num(Reset_column_num[2:0]), .Reset_row_num(Reset_row_num),
    .Reset__x__y(demultiplexer_2_out0), .Screen_OUT(out_7), .Screen_OUT_2(out_8), .Screen_OUT_3(out_9),
    .Screen_OUT_4(out_10), .Screen_OUT_5(out_11), .Screen_OUT_6(out_12), .Screen_OUT_7(out_13),
    .Screen_OUT_8(out_14));
  Display_curcuit__8_bits display_curcuit_8_bits_2 (
    .Y_Positions(Y_positions), .X_Positions(X_positions[2:0]), .Clock(demultiplexer_1_out1),
    .Reset_column_num(Reset_column_num[2:0]), .Reset_row_num(Reset_row_num),
    .Reset__x__y(demultiplexer_2_out1), .Screen_OUT(out_15), .Screen_OUT_2(out_16), .Screen_OUT_3(out_17),
    .Screen_OUT_4(out_18), .Screen_OUT_5(out_19), .Screen_OUT_6(out_20), .Screen_OUT_7(out_21),
    .Screen_OUT_8(out_22));
  Display_curcuit__8_bits display_curcuit_8_bits_3 (
    .Y_Positions(Y_positions), .X_Positions(X_positions[2:0]), .Clock(demultiplexer_1_out2),
    .Reset_column_num(Reset_column_num[2:0]), .Reset_row_num(Reset_row_num),
    .Reset__x__y(demultiplexer_2_out2), .Screen_OUT(out_23), .Screen_OUT_2(out_24), .Screen_OUT_3(out_25),
    .Screen_OUT_4(out_26), .Screen_OUT_5(out_27), .Screen_OUT_6(out_28), .Screen_OUT_7(out_29),
    .Screen_OUT_8(out_30));
  Display_curcuit__8_bits display_curcuit_8_bits_4 (
    .Y_Positions(Y_positions), .X_Positions(X_positions[2:0]), .Clock(demultiplexer_1_out3),
    .Reset_column_num(Reset_column_num[2:0]), .Reset_row_num(Reset_row_num),
    .Reset__x__y(demultiplexer_2_out3), .Screen_OUT(out_31), .Screen_OUT_2(out_32), .Screen_OUT_3(out_33),
    .Screen_OUT_4(out_34), .Screen_OUT_5(out_35), .Screen_OUT_6(out_36), .Screen_OUT_7(out_37),
    .Screen_OUT_8(out_38));
  Demultiplexer #(.select(2)) demultiplexer_2 (
    .out0(demultiplexer_2_out0), .out1(demultiplexer_2_out1), .out2(demultiplexer_2_out2),
    .out3(demultiplexer_2_out3), .in(Reset__x_y), .sel(Reset_column_num[4:3]));  // open: en
endmodule

module Apple_coordinate_digit_display (
  input  [4:0] in_1,
  input  [4:0] in_2,
  output [3:0] out_3,
  output [3:0] out_4,
  output [3:0] out_5,
  output [3:0] out_6
);


  assign out_3 = {3'b000, in_1[4]};
  assign out_4 = in_1[3:0];
  assign out_5 = {3'b000, in_2[4]};
  assign out_6 = in_2[3:0];
endmodule
